// Logisim project Counter.circ as structural Verilog: 2 circuits, main circuit main
module main (
  input  Up_Down
);

  wire clock_1_out;
  wire [2:0] up_down_counter_1_c;

  Clock clock_1 (.out(clock_1_out));
  up_down_counter up_down_counter_1 (
    .X(Up_Down), .Clock(clock_1_out), .out_3(up_down_counter_1_c[2]), .B(up_down_counter_1_c[1]),
    .C(up_down_counter_1_c[0]));
  Hex_Digit_Display hex_digit_display_1 (.value({1'b0, up_down_counter_1_c}));  // open: dp
endmodule

module up_down_counter (
  input  X,
  input  Clock,
  output out_3,
  output B,
  output C
);

  wire A_qn, abc_prime_out, B_qn, C_qn, not_1_out, not_2_out, not_3_out, or_1_out, or_2_out, or_3_out,
       x_prime_a_prime_bc_out, x_prime_ab_prime_out, x_prime_bc_out, x_prime_c_out,
       xa_prime_b_prime_c_prime_out, xac_out, xbc_prime_out, xc_prime_out;

  not not_1 (not_1_out, X);
  and x_prime_ab_prime (x_prime_ab_prime_out, not_1_out, out_3, B_qn);
  and xac (xac_out, X, out_3, C);
  and abc_prime (abc_prime_out, out_3, B, C_qn);
  and xa_prime_b_prime_c_prime (xa_prime_b_prime_c_prime_out, X, A_qn, B_qn, C_qn);
  not not_2 (not_2_out, X);
  and x_prime_a_prime_bc (x_prime_a_prime_bc_out, not_2_out, A_qn, B, C);
  not not_3 (not_3_out, X);
  and x_prime_bc (x_prime_bc_out, not_3_out, B, C);
  and xbc_prime (xbc_prime_out, X, B, C_qn);
  or or_1 (or_1_out, x_prime_ab_prime_out, xac_out, abc_prime_out, xa_prime_b_prime_c_prime_out, x_prime_a_prime_bc_out);
  and x_prime_c (x_prime_c_out, not_3_out, C);
  or or_2 (or_2_out, x_prime_c_out, xc_prime_out);
  and xc_prime (xc_prime_out, X, C_qn);
  or or_3 (or_3_out, x_prime_bc_out, xbc_prime_out);
  D_Flip_Flop A (.clk(Clock), .D(or_1_out), .Q(out_3), .Qn(A_qn));  // open: preset, en, reset
  J_K_Flip_Flop u_B (.J(or_2_out), .clk(Clock), .K(or_3_out), .Q(B), .Qn(B_qn));  // open: preset, en, reset
  T_Flip_Flop u_C (.clk(Clock), .T(1'b1), .Q(C), .Qn(C_qn));  // open: preset, reset, en
endmodule
