// Logisim project lab11.circ as structural Verilog: 11 circuits, main circuit LAB10
module HALF_ADDER (
  input  A,
  input  B,
  output out_3,
  output out_4
);

  xor xor_1 (out_3, A, B);
  and and_1 (out_4, B, A);
endmodule

module FULL_ADDER (
  input  Cin,
  input  A,
  input  B,
  output S,
  output Cout
);

  wire half_adder_1_out_3, half_adder_1_out_4, half_adder_2_out_4;

  HALF_ADDER half_adder_1 (.A(A), .B(B), .out_3(half_adder_1_out_3), .out_4(half_adder_1_out_4));
  HALF_ADDER half_adder_2 (.A(Cin), .B(half_adder_1_out_3), .out_3(S), .out_4(half_adder_2_out_4));
  or or_1 (Cout, half_adder_2_out_4, half_adder_1_out_4);
endmodule

// ADD
module \Ödev  (
  input  [7:0] A,
  input  [7:0] B,
  output Carry,
  output [7:0] Output
);

  wire full_adder_2_cout, full_adder_3_cout, full_adder_4_cout, full_adder_5_cout, full_adder_6_cout,
       full_adder_7_cout, half_adder_1_out_4;

  FULL_ADDER full_adder_1 (.Cin(full_adder_2_cout), .A(B[7]), .B(A[7]), .S(Output[7]), .Cout(Carry));
  FULL_ADDER full_adder_2 (.Cin(full_adder_3_cout), .A(B[6]), .B(A[6]), .S(Output[6]), .Cout(full_adder_2_cout));
  FULL_ADDER full_adder_3 (.Cin(full_adder_4_cout), .A(B[5]), .B(A[5]), .S(Output[5]), .Cout(full_adder_3_cout));
  FULL_ADDER full_adder_4 (.Cin(full_adder_5_cout), .A(B[4]), .B(A[4]), .S(Output[4]), .Cout(full_adder_4_cout));
  FULL_ADDER full_adder_5 (.Cin(full_adder_6_cout), .A(B[3]), .B(A[3]), .S(Output[3]), .Cout(full_adder_5_cout));
  FULL_ADDER full_adder_6 (.Cin(full_adder_7_cout), .A(B[2]), .B(A[2]), .S(Output[2]), .Cout(full_adder_6_cout));
  FULL_ADDER full_adder_7 (.Cin(half_adder_1_out_4), .A(B[1]), .B(A[1]), .S(Output[1]), .Cout(full_adder_7_cout));
  HALF_ADDER half_adder_1 (.A(B[0]), .B(A[0]), .out_3(Output[0]), .out_4(half_adder_1_out_4));

  // Notes on the sheet:
  //   B
  //   A
endmodule

module denemer (
  input  [7:0] A,
  input  [7:0] B,
  input  [2:0] in_3,
  output ZERO,
  output [7:0] OUTPUT
);

  ALU ALU (.A(A), .B(B), .Alu_controller(in_3), .Zero(ZERO), .out_5(OUTPUT));
endmodule

module ALU (
  input  [7:0] A,
  input  [7:0] B,
  input  [2:0] Alu_controller,
  output Zero,
  output [7:0] out_5
);

  wire comparator_1_lt;
  wire [7:0] and_1_out, bit_extender_1_out, bit_extender_2_out, nor_1_out, or_1_out, subtractor_1_out,
       xnor_1_out, xor_1_out, \ödev_1_output ;

  assign and_1_out = A & B;  // AND_Gate and_1, 8 bits wide
  assign or_1_out = A | B;  // OR_Gate or_1, 8 bits wide
  \Ödev  \u_ödev_1  (.A(A), .B(B), .Output(\ödev_1_output ));  // open: Carry
  Subtractor subtractor_1 (.a(A), .b(B), .out(subtractor_1_out));  // open: bin, bout
  Comparator comparator_1 (.a(A), .b(B), .lt(comparator_1_lt));  // open: gt, eq
  assign xor_1_out = A ^ B;  // XOR_Gate xor_1, 8 bits wide
  assign xnor_1_out = ~(A ^ B);  // XNOR_Gate xnor_1, 8 bits wide
  assign nor_1_out = ~(A | B);  // NOR_Gate nor_1, 8 bits wide
  assign bit_extender_1_out = {{7{1'b0}}, comparator_1_lt};  // Bit_Extender bit_extender_1
  Multiplexer #(.select(3), .width(8)) multiplexer_1 (
    .in0(and_1_out), .in1(or_1_out), .in2(\ödev_1_output ), .in3(subtractor_1_out), .in4(bit_extender_1_out),
    .in5(xor_1_out), .in6(xnor_1_out), .in7(nor_1_out), .out(out_5), .sel(Alu_controller));  // open: en
  Comparator comparator_2 (.a(out_5), .b(bit_extender_2_out), .eq(Zero));  // open: gt, lt
  assign bit_extender_2_out = {{7{1'b0}}, 1'b0};  // Bit_Extender bit_extender_2
endmodule

// reg file
module reg_file (
  input  Write_Enable,
  input  Clock,
  input  [7:0] Data,
  input  [2:0] write_adress,
  input  [2:0] readadress,
  input  [2:0] readadres2,
  output [7:0] out_7,
  output [7:0] out_8
);

  wire decoder_1_out0, decoder_1_out1, decoder_1_out2, decoder_1_out3, decoder_1_out4, decoder_1_out5,
       decoder_1_out6, decoder_1_out7;
  wire [7:0] register_1_q, register_2_q, register_3_q, register_4_q, register_5_q, register_6_q,
       register_7_q, register_8_q;

  Decoder #(.select(3), .disabled(0)) decoder_1 (
    .out0(decoder_1_out0), .out1(decoder_1_out1), .out2(decoder_1_out2), .out3(decoder_1_out3),
    .out4(decoder_1_out4), .out5(decoder_1_out5), .out6(decoder_1_out6), .out7(decoder_1_out7),
    .sel(write_adress), .en(Write_Enable));
  Register register_1 (.D(Data), .en(decoder_1_out0), .Q(register_1_q), .clk(Clock));  // open: clr
  Register register_2 (.D(Data), .en(decoder_1_out1), .Q(register_2_q), .clk(Clock));  // open: clr
  Register register_3 (.D(Data), .en(decoder_1_out2), .Q(register_3_q), .clk(Clock));  // open: clr
  Register register_4 (.D(Data), .en(decoder_1_out3), .Q(register_4_q), .clk(Clock));  // open: clr
  Register register_5 (.D(Data), .en(decoder_1_out4), .Q(register_5_q), .clk(Clock));  // open: clr
  Register register_6 (.D(Data), .en(decoder_1_out5), .Q(register_6_q), .clk(Clock));  // open: clr
  Register register_7 (.D(Data), .en(decoder_1_out6), .Q(register_7_q), .clk(Clock));  // open: clr
  Register register_8 (.D(Data), .en(decoder_1_out7), .Q(register_8_q), .clk(Clock));  // open: clr
  Multiplexer #(.select(3), .width(8)) multiplexer_1 (
    .in0(register_1_q), .in1(register_2_q), .in2(register_3_q), .in3(register_4_q), .in4(register_5_q),
    .in5(register_6_q), .in6(register_7_q), .in7(register_8_q), .out(out_7), .sel(readadress));  // open: en
  Multiplexer #(.select(3), .width(8)) multiplexer_2 (
    .in0(register_1_q), .in1(register_2_q), .in2(register_3_q), .in3(register_4_q), .in4(register_5_q),
    .in5(register_6_q), .in6(register_7_q), .in7(register_8_q), .out(out_8), .sel(readadres2));  // open: en
endmodule

module lab9_main (
  input  Clock,
  input  RegWrite,
  input  [7:0] Data,
  input  [2:0] write_adress,
  input  [2:0] read_adress,
  input  [2:0] read_adress2,
  output [7:0] ReadData1,
  output [7:0] ReadData2
);

  reg_file reg_file_1 (
    .Write_Enable(RegWrite), .Clock(Clock), .Data(Data), .write_adress(write_adress),
    .readadress(read_adress), .readadres2(read_adress2), .out_7(ReadData1), .out_8(ReadData2));
endmodule

module Controller (
  input  [3:0] in_1,
  output RedDst,
  output ALUSrc,
  output Jump,
  output MentoReeg,
  output RegWrite,
  output MemRead,
  output MemWrite,
  output Bracnh,
  output AluOp1,
  output AluOp0
);

  wire decoder_1_out8;

  Decoder #(.select(4)) decoder_1 (
    .out0(AluOp1), .out2(Jump), .out3(MemRead), .out4(AluOp0), .out8(decoder_1_out8), .out11(MemWrite));  // open: out1, out5, out6, out7, out9, out10, out12, out13, out14, out15, sel, en
  or or_1 (ALUSrc, MemRead, decoder_1_out8, MemWrite);
  or or_2 (RegWrite, AluOp1, MemRead, decoder_1_out8);

  assign Bracnh = AluOp0;
  assign MentoReeg = MemRead;
  assign RedDst = AluOp1;
endmodule

module LAB10 (
);

  wire alu_1_zero, and_1_out, clock_1_out, newcontrol1_1_alusrc, newcontrol1_1_branch, newcontrol1_1_jump,
       newcontrol1_1_memread, newcontrol1_1_memtoreg, newcontrol1_1_memwrite, newcontrol1_1_regdst,
       newcontrol1_1_regwrite, not_1_out;
  wire [1:0] newcontrol1_1_aluop0;
  wire [2:0] alucontrol_1_out_3, multiplexer_1_out;
  wire [7:0] adder_1_out, adder_2_out, alu_1_out_5, lab9_main_1_readdata1, lab9_main_1_readdata2,
       multiplexer_2_out, multiplexer_3_out, multiplexer_4_out, multiplexer_5_out, ram_1_data, register_1_q;
  wire [17:0] rom_1_data;

  Register register_1 (.D(multiplexer_4_out), .Q(register_1_q), .clk(clock_1_out));  // open: en, clr
  Adder adder_1 (.a(8'h1), .b(register_1_q), .out(adder_1_out));  // open: cin, cout
  ROM #(.dataWidth(18)) rom_1 (.addr(register_1_q), .data(rom_1_data));  // open: sel
  Clock clock_1 (.out(clock_1_out));
  Multiplexer #(.width(3)) multiplexer_1 (
    .in0(rom_1_data[10:8]), .in1(rom_1_data[7:5]), .out(multiplexer_1_out), .sel(newcontrol1_1_regdst));  // open: en
  NewControl1 newcontrol1_1 (
    .in_1(rom_1_data[17:14]), .RegDst(newcontrol1_1_regdst), .ALUSrc(newcontrol1_1_alusrc),
    .Jump(newcontrol1_1_jump), .MemtoReg(newcontrol1_1_memtoreg), .RegWrite(newcontrol1_1_regwrite),
    .MemRead(newcontrol1_1_memread), .MemWrite(newcontrol1_1_memwrite), .Branch(newcontrol1_1_branch),
    .ALUOp1(newcontrol1_1_aluop0[1]), .ALUOp0(newcontrol1_1_aluop0[0]));
  lab9_main lab9_main_1 (
    .RegWrite(newcontrol1_1_regwrite), .Data(multiplexer_5_out), .write_adress(multiplexer_1_out),
    .read_adress(rom_1_data[13:11]), .read_adress2(rom_1_data[10:8]), .ReadData1(lab9_main_1_readdata1),
    .ReadData2(lab9_main_1_readdata2), .Clock(clock_1_out));
  AluControl alucontrol_1 (.AluOP(newcontrol1_1_aluop0), .Function(rom_1_data[2:0]), .out_3(alucontrol_1_out_3));
  Adder adder_2 (.a(adder_1_out), .b(rom_1_data[7:0]), .out(adder_2_out));  // open: cin, cout
  Multiplexer #(.width(8)) multiplexer_2 (
    .in0(lab9_main_1_readdata2), .in1(rom_1_data[7:0]), .out(multiplexer_2_out), .sel(newcontrol1_1_alusrc));  // open: en
  Multiplexer #(.width(8)) multiplexer_3 (
    .in0(adder_1_out), .in1(adder_2_out), .out(multiplexer_3_out), .sel(and_1_out));  // open: en
  and and_1 (and_1_out, newcontrol1_1_branch, alu_1_zero);
  ALU alu_1 (
    .A(lab9_main_1_readdata1), .B(multiplexer_2_out), .Alu_controller(alucontrol_1_out_3), .Zero(alu_1_zero),
    .out_5(alu_1_out_5));
  Multiplexer #(.width(8)) multiplexer_4 (
    .in0(multiplexer_3_out), .in1(rom_1_data[7:0]), .out(multiplexer_4_out), .sel(newcontrol1_1_jump));  // open: en
  RAM #(.bus("separate")) ram_1 (
    .addr(alu_1_out_5), .din(lab9_main_1_readdata2), .data(ram_1_data), .str(newcontrol1_1_memwrite),
    .clk(not_1_out), .ld(newcontrol1_1_memread));  // open: sel, clr
  not not_1 (not_1_out, clock_1_out);
  Multiplexer #(.width(8)) multiplexer_5 (
    .in0(alu_1_out_5), .in1(ram_1_data), .out(multiplexer_5_out), .sel(newcontrol1_1_memtoreg));  // open: en

  // Notes on the sheet:
  //   contents of rom_1 (hex, n*v repeats v):
  //   2010f 20218 a62 a83 aa0 ac1 ae5 2c101 2c202 2c303 2c404 2c505 2c606 2c707
endmodule

module NewControl1 (
  input  [3:0] in_1,
  output RegDst,
  output ALUSrc,
  output Jump,
  output MemtoReg,
  output RegWrite,
  output MemRead,
  output MemWrite,
  output Branch,
  output ALUOp1,
  output ALUOp0
);

  wire and_4_out, and_5_out, not_1_out, not_2_out, not_3_out, not_4_out, not_5_out, not_6_out, not_7_out,
       not_8_out, not_9_out, not_10_out;

  not not_1 (not_1_out, in_1[3]);
  not not_2 (not_2_out, in_1[1]);
  or or_1 (ALUSrc, in_1[1], in_1[3]);
  not not_3 (not_3_out, in_1[0]);
  not not_4 (not_4_out, in_1[2]);
  not not_5 (not_5_out, in_1[1]);
  not not_6 (not_6_out, in_1[3]);
  not not_7 (not_7_out, in_1[3]);
  and and_1 (MemWrite, in_1[3], in_1[1]);
  not not_8 (not_8_out, in_1[3]);
  not not_9 (not_9_out, in_1[2]);
  not not_10 (not_10_out, in_1[1]);
  and and_2 (RegDst, not_1_out, not_2_out);
  and and_3 (Jump, in_1[1], not_3_out);
  and and_4 (and_4_out, not_4_out, not_5_out);
  and and_5 (and_5_out, not_6_out, in_1[0]);
  and and_6 (MemRead, not_7_out, in_1[0]);
  and and_7 (ALUOp1, not_8_out, not_9_out, not_10_out);
  or or_2 (RegWrite, and_4_out, and_5_out);

  assign ALUOp0 = in_1[2];
  assign Branch = in_1[2];
  assign MemtoReg = in_1[1];
endmodule

module AluControl (
  input  [1:0] AluOP,
  input  [2:0] Function,
  output [2:0] out_3
);

  wire and_2_out, not_1_out;

  and and_1 (out_3[2], AluOP[1], Function[2]);
  not not_1 (not_1_out, AluOP[1]);
  and and_2 (and_2_out, AluOP[1], Function[0]);
  or or_1 (out_3[1], not_1_out, Function[1]);
  or or_2 (out_3[0], AluOP[0], and_2_out);
endmodule
