// Logisim project Lab11s1.circ as structural Verilog: 1 circuit, main circuit lab9
// A
module lab9 (
  output Q_A,
  output Q_B,
  output Q_C,
  output Q_D
);

  wire A_qn, clock_1_out, decoder_1_out0, decoder_1_out3, decoder_1_out4, decoder_1_out5, multiplexer_1_out,
       not_2_out, or_1_out, xnor_1_out;
  wire [2:0] not_1_out;

  not not_1 (not_1_out[0], A_qn);
  Multiplexer #(.select(3)) multiplexer_1 (
    .in0(1'b1), .in1(Q_D), .in2(A_qn), .in3(1'b0), .in4(1'b0), .in5(1'b1), .in6(1'b0),
    .out(multiplexer_1_out), .sel({not_1_out[2], Q_C, not_1_out[0]}));  // open: in7, en
  Decoder #(.select(3)) decoder_1 (
    .out0(decoder_1_out0), .out3(decoder_1_out3), .out4(decoder_1_out4), .out5(decoder_1_out5),
    .sel({not_1_out[2], Q_C, not_1_out[0]}));  // open: out1, out2, out6, out7, en
  or or_1 (or_1_out, decoder_1_out0, decoder_1_out3, decoder_1_out4, decoder_1_out5, Q_C);
  not not_2 (not_2_out, multiplexer_1_out);
  xnor xnor_1 (xnor_1_out, multiplexer_1_out, or_1_out);
  Clock clock_1 (.out(clock_1_out));
  D_Flip_Flop A (.clk(clock_1_out), .D(multiplexer_1_out), .Q(Q_A), .Qn(A_qn));  // open: preset, en, reset
  T_Flip_Flop B (.clk(clock_1_out), .T(or_1_out), .Q(Q_B), .Qn(not_1_out[2]));  // open: preset, reset, en
  J_K_Flip_Flop C (.J(not_2_out), .clk(clock_1_out), .K(xnor_1_out), .Q(Q_C));  // open: Qn, preset, en, reset
  D_Flip_Flop D (.clk(clock_1_out), .D(not_1_out[2]), .Q(Q_D));  // open: Qn, preset, en, reset
endmodule
