// Logisim project Lab8(compare-multipy).circ as structural Verilog: 8 circuits, main circuit main
module main (
  input  [7:0] B,
  input  [7:0] A,
  output A_B,
  output A_B_2,
  output A_B_3
);

  Hex_Digit_Display hex_digit_display_1 (.value(A[7:4]));  // open: dp
  Hex_Digit_Display hex_digit_display_2 (.value(A[3:0]));  // open: dp
  _8_bit_compare u_8_bit_compare_1 (.A(A), .B(B), .A_B(A_B), .A_B_2(A_B_2), .B_A(A_B_3));
  Hex_Digit_Display hex_digit_display_3 (.value(B[3:0]));  // open: dp
  Hex_Digit_Display hex_digit_display_4 (.value(B[7:4]));  // open: dp

  // Notes on the sheet:
  //   20070001007
  //   Efe İlhan
endmodule

// HA
module Half_adder (
  input  A,
  input  B,
  output Sum,
  output Carry
);

  xor xor_1 (Sum, A, B);
  and and_1 (Carry, A, B);
endmodule

// FA
module Full_Adder (
  input  A,
  input  B,
  input  Carry,
  output Sum,
  output Cout
);

  wire and_1_out, half_adder_1_carry, half_adder_1_sum;

  Half_adder half_adder_1 (.A(A), .B(B), .Sum(half_adder_1_sum), .Carry(half_adder_1_carry));
  xor xor_1 (Sum, half_adder_1_sum, Carry);
  and and_1 (and_1_out, half_adder_1_sum, Carry);
  or or_1 (Cout, and_1_out, half_adder_1_carry);
endmodule

// 2bit 4 adder
module _2_bit_plus_4_bit_adder (
  input  A1,
  input  A0,
  input  B0,
  input  B1,
  input  b2,
  input  b3,
  output a1_2,
  output out_8,
  output out_9,
  output out_10
);

  wire full_adder_1_cout, half_adder_1_carry, half_adder_2_carry;

  Half_adder half_adder_1 (.A(A0), .B(B0), .Sum(a1_2), .Carry(half_adder_1_carry));
  Full_Adder full_adder_1 (.A(half_adder_1_carry), .B(A1), .Carry(B1), .Sum(out_8), .Cout(full_adder_1_cout));
  Half_adder half_adder_2 (.A(full_adder_1_cout), .B(b2), .Sum(out_9), .Carry(half_adder_2_carry));
  Half_adder half_adder_3 (.A(half_adder_2_carry), .B(b3), .Sum(out_10));  // open: Carry
endmodule

// 2x2
module _2_bit_by_2_bit_multiplier (
  input  A0,
  input  A1,
  input  B0,
  input  b1,
  output C0,
  output c1,
  output c2,
  output c3
);

  wire and_2_out, and_3_out, and_4_out, half_adder_1_carry;

  and and_1 (C0, A0, B0);
  and and_2 (and_2_out, A0, b1);
  and and_3 (and_3_out, A1, B0);
  and and_4 (and_4_out, A1, b1);
  Half_adder half_adder_1 (.A(and_2_out), .B(and_3_out), .Sum(c1), .Carry(half_adder_1_carry));
  Half_adder half_adder_2 (.A(half_adder_1_carry), .B(and_4_out), .Sum(c2), .Carry(c3));
endmodule

module _4_bit_by_4_bit_multiplier (
  input  [3:0] A,
  input  [3:0] B,
  output out_3,
  output out_4,
  output out_5,
  output out_6,
  output out_7,
  output out_8,
  output out_9,
  output out_10
);

  wire n2_bit_by_2_bit_multiplier_1_c2, n2_bit_by_2_bit_multiplier_1_c3, n2_bit_by_2_bit_multiplier_2_c0,
       n2_bit_by_2_bit_multiplier_2_c1, n2_bit_by_2_bit_multiplier_2_c2, n2_bit_by_2_bit_multiplier_2_c3,
       n2_bit_by_2_bit_multiplier_3_c0, n2_bit_by_2_bit_multiplier_3_c1, n2_bit_by_2_bit_multiplier_3_c2,
       n2_bit_by_2_bit_multiplier_3_c3, n2_bit_by_2_bit_multiplier_4_c0, n2_bit_by_2_bit_multiplier_4_c1,
       n2_bit_by_2_bit_multiplier_4_c2, n2_bit_by_2_bit_multiplier_4_c3, n2_bit_plus_4_bit_adder_1_a1_2,
       n2_bit_plus_4_bit_adder_1_out_8, n2_bit_plus_4_bit_adder_1_out_9, n2_bit_plus_4_bit_adder_1_out_10,
       n2_bit_plus_4_bit_adder_2_a1_2, n2_bit_plus_4_bit_adder_2_out_8, n2_bit_plus_4_bit_adder_2_out_9,
       n2_bit_plus_4_bit_adder_2_out_10, n2_bit_plus_4_bit_adder_3_out_9, n2_bit_plus_4_bit_adder_3_out_10;

  _2_bit_by_2_bit_multiplier u_2_bit_by_2_bit_multiplier_1 (
    .A0(A[0]), .A1(A[1]), .B0(B[0]), .b1(B[1]), .C0(out_3), .c1(out_4), .c2(n2_bit_by_2_bit_multiplier_1_c2),
    .c3(n2_bit_by_2_bit_multiplier_1_c3));
  _2_bit_by_2_bit_multiplier u_2_bit_by_2_bit_multiplier_2 (
    .A0(A[0]), .A1(A[1]), .B0(B[2]), .b1(B[3]), .C0(n2_bit_by_2_bit_multiplier_2_c0),
    .c1(n2_bit_by_2_bit_multiplier_2_c1), .c2(n2_bit_by_2_bit_multiplier_2_c2),
    .c3(n2_bit_by_2_bit_multiplier_2_c3));
  _2_bit_by_2_bit_multiplier u_2_bit_by_2_bit_multiplier_3 (
    .A0(A[2]), .A1(A[3]), .B0(B[1]), .b1(B[0]), .C0(n2_bit_by_2_bit_multiplier_3_c0),
    .c1(n2_bit_by_2_bit_multiplier_3_c1), .c2(n2_bit_by_2_bit_multiplier_3_c2),
    .c3(n2_bit_by_2_bit_multiplier_3_c3));
  _2_bit_by_2_bit_multiplier u_2_bit_by_2_bit_multiplier_4 (
    .A0(A[2]), .A1(A[3]), .B0(B[2]), .b1(B[3]), .C0(n2_bit_by_2_bit_multiplier_4_c0),
    .c1(n2_bit_by_2_bit_multiplier_4_c1), .c2(n2_bit_by_2_bit_multiplier_4_c2),
    .c3(n2_bit_by_2_bit_multiplier_4_c3));
  _2_bit_plus_4_bit_adder u_2_bit_plus_4_bit_adder_1 (
    .B0(n2_bit_by_2_bit_multiplier_2_c3), .B1(n2_bit_by_2_bit_multiplier_2_c2),
    .b2(n2_bit_by_2_bit_multiplier_2_c1), .b3(n2_bit_by_2_bit_multiplier_2_c0),
    .A1(n2_bit_by_2_bit_multiplier_1_c3), .A0(n2_bit_by_2_bit_multiplier_1_c2),
    .a1_2(n2_bit_plus_4_bit_adder_1_a1_2), .out_8(n2_bit_plus_4_bit_adder_1_out_8),
    .out_9(n2_bit_plus_4_bit_adder_1_out_9), .out_10(n2_bit_plus_4_bit_adder_1_out_10));
  _2_bit_plus_4_bit_adder u_2_bit_plus_4_bit_adder_2 (
    .B0(n2_bit_by_2_bit_multiplier_4_c3), .B1(n2_bit_by_2_bit_multiplier_4_c2),
    .b2(n2_bit_by_2_bit_multiplier_4_c1), .b3(n2_bit_by_2_bit_multiplier_4_c0),
    .A1(n2_bit_by_2_bit_multiplier_3_c3), .A0(n2_bit_by_2_bit_multiplier_3_c2),
    .a1_2(n2_bit_plus_4_bit_adder_2_a1_2), .out_8(n2_bit_plus_4_bit_adder_2_out_8),
    .out_9(n2_bit_plus_4_bit_adder_2_out_9), .out_10(n2_bit_plus_4_bit_adder_2_out_10));
  _2_bit_plus_4_bit_adder u_2_bit_plus_4_bit_adder_3 (
    .B0(n2_bit_plus_4_bit_adder_1_out_10), .B1(n2_bit_plus_4_bit_adder_1_out_9),
    .b2(n2_bit_plus_4_bit_adder_1_out_8), .b3(n2_bit_plus_4_bit_adder_1_a1_2),
    .A1(n2_bit_by_2_bit_multiplier_3_c1), .A0(n2_bit_by_2_bit_multiplier_3_c0), .a1_2(out_5), .out_8(out_6),
    .out_9(n2_bit_plus_4_bit_adder_3_out_9), .out_10(n2_bit_plus_4_bit_adder_3_out_10));
  _2_bit_plus_4_bit_adder u_2_bit_plus_4_bit_adder_4 (
    .B0(n2_bit_plus_4_bit_adder_2_out_10), .B1(n2_bit_plus_4_bit_adder_2_out_9),
    .b2(n2_bit_plus_4_bit_adder_2_out_8), .b3(n2_bit_plus_4_bit_adder_2_a1_2),
    .A1(n2_bit_plus_4_bit_adder_3_out_10), .A0(n2_bit_plus_4_bit_adder_3_out_9), .a1_2(out_7), .out_8(out_8),
    .out_9(out_9), .out_10(out_10));
endmodule

module _4_bit_magnitude_comparator (
  input  A3,
  input  B3,
  input  A2,
  input  B2,
  input  A1,
  input  B1,
  input  A0,
  input  B0,
  output A_B,
  output A_B_2,
  output A_B_3
);

  wire and_1_out, and_2_out, and_3_out, and_4_out, and_5_out, and_6_out, and_7_out, and_8_out, and_9_out,
       and_10_out, and_11_out, and_12_out, and_13_out, and_14_out, nor_1_out, nor_2_out, nor_3_out,
       nor_4_out, not_1_out, not_2_out, not_3_out, not_4_out, not_5_out, not_6_out, not_7_out, not_8_out;

  not not_1 (not_1_out, A3);
  not not_2 (not_2_out, B3);
  not not_3 (not_3_out, A2);
  not not_4 (not_4_out, B2);
  not not_5 (not_5_out, A1);
  not not_6 (not_6_out, B1);
  not not_7 (not_7_out, A0);
  not not_8 (not_8_out, B0);
  and and_1 (and_1_out, not_1_out, B3);
  and and_2 (and_2_out, A3, not_2_out);
  and and_3 (and_3_out, not_3_out, B2);
  and and_4 (and_4_out, A2, not_4_out);
  and and_5 (and_5_out, not_5_out, B1);
  and and_6 (and_6_out, A1, not_6_out);
  and and_7 (and_7_out, not_7_out, B0);
  and and_8 (and_8_out, A0, not_8_out);
  nor nor_1 (nor_1_out, and_1_out, and_2_out);
  nor nor_2 (nor_2_out, and_3_out, and_4_out);
  nor nor_3 (nor_3_out, and_5_out, and_6_out);
  nor nor_4 (nor_4_out, and_7_out, and_8_out);
  and and_9 (and_9_out, nor_1_out, and_3_out);
  and and_10 (and_10_out, nor_1_out, and_4_out);
  and and_11 (and_11_out, nor_1_out, nor_2_out, and_5_out);
  and and_12 (and_12_out, nor_1_out, nor_2_out, and_6_out);
  and and_13 (and_13_out, nor_1_out, nor_2_out, nor_3_out, and_7_out);
  and and_14 (and_14_out, nor_1_out, nor_2_out, nor_3_out, and_8_out);
  and and_15 (A_B_3, nor_1_out, nor_2_out, nor_3_out, nor_4_out);
  or or_1 (A_B, and_1_out, and_9_out, and_11_out, and_13_out);
  or or_2 (A_B_2, and_2_out, and_10_out, and_12_out, and_14_out);
endmodule

// 8-bit compare
module _8_bit_compare (
  input  [7:0] A,
  input  [7:0] B,
  output A_B,
  output A_B_2,
  output B_A
);

  wire and_1_out, and_3_out, n4_bit_magnitude_comparator_1_a_b, n4_bit_magnitude_comparator_1_a_b_2,
       n4_bit_magnitude_comparator_1_a_b_3, n4_bit_magnitude_comparator_2_a_b,
       n4_bit_magnitude_comparator_2_a_b_2, n4_bit_magnitude_comparator_2_a_b_3;

  _4_bit_magnitude_comparator u_4_bit_magnitude_comparator_1 (
    .A3(A[7]), .B3(B[7]), .A2(A[6]), .B2(B[6]), .A1(A[5]), .B1(B[5]), .A0(A[4]), .B0(B[4]),
    .A_B(n4_bit_magnitude_comparator_1_a_b), .A_B_2(n4_bit_magnitude_comparator_1_a_b_2),
    .A_B_3(n4_bit_magnitude_comparator_1_a_b_3));
  _4_bit_magnitude_comparator u_4_bit_magnitude_comparator_2 (
    .A3(A[3]), .B3(B[3]), .A2(A[2]), .B2(B[2]), .A1(A[1]), .B1(B[1]), .A0(A[0]), .B0(B[0]),
    .A_B(n4_bit_magnitude_comparator_2_a_b), .A_B_2(n4_bit_magnitude_comparator_2_a_b_2),
    .A_B_3(n4_bit_magnitude_comparator_2_a_b_3));
  and and_1 (and_1_out, n4_bit_magnitude_comparator_1_a_b_3, n4_bit_magnitude_comparator_2_a_b_2);
  and and_2 (A_B_2, n4_bit_magnitude_comparator_1_a_b_3, n4_bit_magnitude_comparator_2_a_b_3);
  and and_3 (and_3_out, n4_bit_magnitude_comparator_1_a_b_3, n4_bit_magnitude_comparator_2_a_b);
  or or_1 (A_B, n4_bit_magnitude_comparator_1_a_b_2, and_1_out);
  or or_2 (B_A, and_3_out, n4_bit_magnitude_comparator_1_a_b);
endmodule
