// Logisim project efeilhan_lab09.circ as structural Verilog: 6 circuits, main circuit main
module main (
  input  [3:0] in_1,
  input  [1:0] in_2
);

  wire [3:0] controller_1_out_3;

  Controller controller_1 (._4BIT(in_1), ._2BIT(in_2), .out_3(controller_1_out_3));
  Hex_Digit_Display hex_digit_display_1 (.value(controller_1_out_3));  // open: dp
endmodule

module _3_8_decoder (
  input  E,
  input  A2,
  input  A1,
  input  A0,
  output Z7,
  output Z6,
  output Z5,
  output Z4,
  output Z3,
  output Z2,
  output Z1,
  output Z0
);

  wire not_1_out, not_2_out, not_3_out;

  not not_1 (not_1_out, A2);
  not not_2 (not_2_out, A1);
  not not_3 (not_3_out, A0);
  and and_1 (Z7, A0, A1, A2, E);
  and and_2 (Z6, A2, A1, not_3_out, E);
  and and_3 (Z5, A2, not_2_out, A0, E);
  and and_4 (Z4, A2, not_2_out, not_3_out, E);
  and and_5 (Z3, not_1_out, A1, A0, E);
  and and_6 (Z2, not_1_out, A1, not_3_out, E);
  and and_7 (Z1, not_1_out, not_2_out, A0, E);
  and and_8 (Z0, not_1_out, not_2_out, not_3_out, E);
endmodule

module _4_1_multiplexer (
  input  K0,
  input  K1,
  input  K2,
  input  K3,
  input  S1,
  input  S0,
  output out_7
);

  wire and_1_out, and_2_out, and_3_out, and_4_out, not_1_out, not_2_out;

  not not_1 (not_1_out, S1);
  not not_2 (not_2_out, S0);
  and and_1 (and_1_out, K0, not_1_out, not_2_out);
  and and_2 (and_2_out, K1, not_1_out, S0);
  and and_3 (and_3_out, K2, S1, not_2_out);
  and and_4 (and_4_out, K3, S1, S0);
  or or_1 (out_7, and_1_out, and_2_out, and_3_out, and_4_out);
endmodule

module _4_16_decoder_using_3_8 (
  input  A,
  input  B,
  input  C,
  input  E,
  output A0,
  output out_6,
  output out_7,
  output out_8,
  output out_9,
  output out_10,
  output out_11,
  output out_12,
  output out_13,
  output out_14,
  output out_15,
  output out_16,
  output out_17,
  output out_18,
  output out_19,
  output A15
);

  wire not_1_out;

  not not_1 (not_1_out, E);
  _3_8_decoder u_3_8_decoder_1 (
    .E(not_1_out), .A2(C), .A1(B), .A0(A), .Z7(out_12), .Z6(out_11), .Z5(out_10), .Z4(out_9), .Z3(out_8),
    .Z2(out_7), .Z1(out_6), .Z0(A0));
  _3_8_decoder u_3_8_decoder_2 (
    .E(E), .A2(C), .A1(B), .A0(A), .Z7(A15), .Z6(out_19), .Z5(out_18), .Z4(out_17), .Z3(out_16), .Z2(out_15),
    .Z1(out_14), .Z0(out_13));
endmodule

module Excess_3_convertor (
  input  B3,
  input  B2,
  input  B1,
  input  B0,
  output E3,
  output E2,
  output E1,
  output E0
);

  wire n4_16_decoder_using_3_8_1_a0, n4_16_decoder_using_3_8_1_a15, n4_16_decoder_using_3_8_1_out_6,
       n4_16_decoder_using_3_8_1_out_7, n4_16_decoder_using_3_8_1_out_8, n4_16_decoder_using_3_8_1_out_9,
       n4_16_decoder_using_3_8_1_out_10, n4_16_decoder_using_3_8_1_out_11, n4_16_decoder_using_3_8_1_out_12,
       n4_16_decoder_using_3_8_1_out_13, n4_16_decoder_using_3_8_1_out_14, n4_16_decoder_using_3_8_1_out_15,
       n4_16_decoder_using_3_8_1_out_16, n4_16_decoder_using_3_8_1_out_17, n4_16_decoder_using_3_8_1_out_18,
       n4_16_decoder_using_3_8_1_out_19;

  _4_16_decoder_using_3_8 u_4_16_decoder_using_3_8_1 (
    .A(B0), .B(B1), .C(B2), .E(B3), .A0(n4_16_decoder_using_3_8_1_a0),
    .out_6(n4_16_decoder_using_3_8_1_out_6), .out_7(n4_16_decoder_using_3_8_1_out_7),
    .out_8(n4_16_decoder_using_3_8_1_out_8), .out_9(n4_16_decoder_using_3_8_1_out_9),
    .out_10(n4_16_decoder_using_3_8_1_out_10), .out_11(n4_16_decoder_using_3_8_1_out_11),
    .out_12(n4_16_decoder_using_3_8_1_out_12), .out_13(n4_16_decoder_using_3_8_1_out_13),
    .out_14(n4_16_decoder_using_3_8_1_out_14), .out_15(n4_16_decoder_using_3_8_1_out_15),
    .out_16(n4_16_decoder_using_3_8_1_out_16), .out_17(n4_16_decoder_using_3_8_1_out_17),
    .out_18(n4_16_decoder_using_3_8_1_out_18), .out_19(n4_16_decoder_using_3_8_1_out_19),
    .A15(n4_16_decoder_using_3_8_1_a15));
  or or_1 (E3, n4_16_decoder_using_3_8_1_out_10, n4_16_decoder_using_3_8_1_out_11, n4_16_decoder_using_3_8_1_out_12, n4_16_decoder_using_3_8_1_out_13, n4_16_decoder_using_3_8_1_out_14);
  or or_2 (E2, n4_16_decoder_using_3_8_1_out_6, n4_16_decoder_using_3_8_1_out_7, n4_16_decoder_using_3_8_1_out_8, n4_16_decoder_using_3_8_1_out_9, n4_16_decoder_using_3_8_1_out_14);
  or or_3 (E1, n4_16_decoder_using_3_8_1_a0, n4_16_decoder_using_3_8_1_out_8, n4_16_decoder_using_3_8_1_out_9, n4_16_decoder_using_3_8_1_out_12, n4_16_decoder_using_3_8_1_out_13);
  or or_4 (E0, n4_16_decoder_using_3_8_1_a0, n4_16_decoder_using_3_8_1_out_7, n4_16_decoder_using_3_8_1_out_9, n4_16_decoder_using_3_8_1_out_11, n4_16_decoder_using_3_8_1_out_13);
endmodule

module Controller (
  input  [3:0] _4BIT,
  input  [1:0] _2BIT,
  output [3:0] out_3
);

  wire excess_3_convertor_1_e0, excess_3_convertor_1_e1, excess_3_convertor_1_e2, excess_3_convertor_1_e3,
       not_1_out, not_2_out, not_3_out, not_4_out, or_1_out, or_2_out, or_3_out, or_4_out;

  Excess_3_convertor excess_3_convertor_1 (
    .B3(_4BIT[3]), .B2(_4BIT[2]), .B1(_4BIT[1]), .B0(_4BIT[0]), .E3(excess_3_convertor_1_e3),
    .E2(excess_3_convertor_1_e2), .E1(excess_3_convertor_1_e1), .E0(excess_3_convertor_1_e0));
  not not_1 (not_1_out, _4BIT[0]);
  not not_2 (not_2_out, _4BIT[1]);
  not not_3 (not_3_out, _4BIT[2]);
  not not_4 (not_4_out, _4BIT[3]);
  or or_1 (or_1_out, excess_3_convertor_1_e0, _4BIT[0]);
  or or_2 (or_2_out, excess_3_convertor_1_e1, _4BIT[1]);
  or or_3 (or_3_out, excess_3_convertor_1_e2, _4BIT[2]);
  or or_4 (or_4_out, excess_3_convertor_1_e3, _4BIT[3]);
  _4_1_multiplexer u_4_1_multiplexer_1 (
    .K0(_4BIT[0]), .K1(excess_3_convertor_1_e0), .K2(not_1_out), .K3(or_1_out), .S1(_2BIT[1]), .S0(_2BIT[0]),
    .out_7(out_3[0]));
  _4_1_multiplexer u_4_1_multiplexer_2 (
    .K0(_4BIT[1]), .K1(excess_3_convertor_1_e1), .K2(not_2_out), .K3(or_2_out), .S1(_2BIT[1]), .S0(_2BIT[0]),
    .out_7(out_3[1]));
  _4_1_multiplexer u_4_1_multiplexer_3 (
    .K0(_4BIT[2]), .K1(excess_3_convertor_1_e2), .K2(not_3_out), .K3(or_3_out), .S1(_2BIT[1]), .S0(_2BIT[0]),
    .out_7(out_3[2]));
  _4_1_multiplexer u_4_1_multiplexer_4 (
    .K0(_4BIT[3]), .K1(excess_3_convertor_1_e3), .K2(not_4_out), .K3(or_4_out), .S1(_2BIT[1]), .S0(_2BIT[0]),
    .out_7(out_3[3]));
endmodule
