// Logisim project lab13skeleton.circ as structural Verilog: 2 circuits, main circuit Main
module Main (
  input  [7:0] Input,
  input  Load_Shift,
  output Detected
);

  wire Clk_out, not_1_out, shift_register_1_out;

  Clock Clk (.out(Clk_out));
  not not_1 (not_1_out, Load_Shift);
  Shift_Register shift_register_1 (
    .shift(not_1_out), .in(1'b0), .clk(Clk_out), .out(shift_register_1_out), .load(Load_Shift),
    .d0(Input[0]), .d1(Input[1]), .d2(Input[2]), .d3(Input[3]), .d4(Input[4]), .d5(Input[5]), .d6(Input[6]),
    .d7(Input[7]));  // open: clr, q0, q1, q2, q3, q4, q5, q6, q7
  Detector detector_1 (.\input (shift_register_1_out), .\output (Detected), .CLK(Clk_out));

  // Notes on the sheet:
  //   0 input
endmodule

module Detector (
  input  \input ,
  input  CLK,
  output \output 
);

  wire and_1_out, and_2_out, not_1_out, not_2_out, or_1_out, or_2_out, T1_q, t2_q, t2_qn;

  not not_1 (not_1_out, \input );
  T_Flip_Flop T1 (.clk(CLK), .T(or_1_out), .Q(T1_q));  // open: Qn, preset, reset, en
  T_Flip_Flop t2 (.clk(CLK), .T(or_2_out), .Q(t2_q), .Qn(t2_qn));  // open: preset, reset, en
  and and_1 (and_1_out, t2_q, not_2_out);
  not not_2 (not_2_out, \input );
  or or_1 (or_1_out, t2_q, T1_q);
  and and_2 (and_2_out, t2_qn, \input );
  or or_2 (or_2_out, and_2_out, and_1_out);
  and and_3 (\output , T1_q, not_1_out, t2_q);
endmodule
