// Logisim project lab8.circ as structural Verilog: 4 circuits, main circuit HALF ADDER 
module HALF_ADDER (
  input  A,
  input  B,
  output out_3,
  output out_4
);

  xor xor_1 (out_3, A, B);
  and and_1 (out_4, B, A);
endmodule

module FULL_ADDER (
  input  Cin,
  input  A,
  input  B,
  output S,
  output Cout
);

  wire half_adder_1_out_3, half_adder_1_out_4, half_adder_2_out_4;

  HALF_ADDER half_adder_1 (.A(A), .B(B), .out_3(half_adder_1_out_3), .out_4(half_adder_1_out_4));
  HALF_ADDER half_adder_2 (.A(Cin), .B(half_adder_1_out_3), .out_3(S), .out_4(half_adder_2_out_4));
  or or_1 (Cout, half_adder_2_out_4, half_adder_1_out_4);
endmodule

module \Ödev  (
  input  [7:0] in_1,
  input  [7:0] in_2,
  output Carry,
  output [7:0] out_4
);

  wire full_adder_2_cout, full_adder_3_cout, full_adder_4_cout, full_adder_5_cout, full_adder_6_cout,
       full_adder_7_cout, half_adder_1_out_4;

  FULL_ADDER full_adder_1 (.Cin(full_adder_2_cout), .A(in_2[7]), .B(in_1[7]), .S(out_4[7]), .Cout(Carry));
  FULL_ADDER full_adder_2 (.Cin(full_adder_3_cout), .A(in_2[6]), .B(in_1[6]), .S(out_4[6]), .Cout(full_adder_2_cout));
  FULL_ADDER full_adder_3 (.Cin(full_adder_4_cout), .A(in_2[5]), .B(in_1[5]), .S(out_4[5]), .Cout(full_adder_3_cout));
  FULL_ADDER full_adder_4 (.Cin(full_adder_5_cout), .A(in_2[4]), .B(in_1[4]), .S(out_4[4]), .Cout(full_adder_4_cout));
  FULL_ADDER full_adder_5 (.Cin(full_adder_6_cout), .A(in_2[3]), .B(in_1[3]), .S(out_4[3]), .Cout(full_adder_5_cout));
  FULL_ADDER full_adder_6 (.Cin(full_adder_7_cout), .A(in_2[2]), .B(in_1[2]), .S(out_4[2]), .Cout(full_adder_6_cout));
  FULL_ADDER full_adder_7 (.Cin(half_adder_1_out_4), .A(in_2[1]), .B(in_1[1]), .S(out_4[1]), .Cout(full_adder_7_cout));
  HALF_ADDER half_adder_1 (.A(in_2[0]), .B(in_1[0]), .out_3(out_4[0]), .out_4(half_adder_1_out_4));

  // Notes on the sheet:
  //   B
  //   A
endmodule

module denemer (
  input  [7:0] in_1,
  input  [7:0] in_2,
  output [7:0] out_3,
  output Overflow_bit
);

  \Ödev  \u_ödev_1  (.in_1(in_1), .in_2(in_2), .Carry(Overflow_bit), .out_4(out_3));
endmodule
