// Logisim project labwork7.circ as structural Verilog: 3 circuits, main circuit main
module main (
  input  [3:0] in_1,
  input  [3:0] _7_as_input
);

  wire exces_2_converter_1_w, exces_2_converter_1_x, exces_2_converter_1_y, exces_2_converter_1_z,
       n7_segment_driveri_1_a_2, n7_segment_driveri_1_b_2, n7_segment_driveri_1_c_2,
       n7_segment_driveri_1_d_2, n7_segment_driveri_1_e, n7_segment_driveri_1_f, n7_segment_driveri_1_g,
       n7_segment_driveri_2_a_2, n7_segment_driveri_2_b_2, n7_segment_driveri_2_c_2,
       n7_segment_driveri_2_d_2, n7_segment_driveri_2_e, n7_segment_driveri_2_f, n7_segment_driveri_2_g;

  Exces_2_converter exces_2_converter_1 (
    .A(in_1[3]), .B(in_1[2]), .C(in_1[1]), .D(in_1[0]), .W(exces_2_converter_1_w), .X(exces_2_converter_1_x),
    .Y(exces_2_converter_1_y), .Z(exces_2_converter_1_z));
  _7_segment_driveri u_7_segment_driveri_1 (
    .D(exces_2_converter_1_w), .C(exces_2_converter_1_x), .B(exces_2_converter_1_y),
    .A(exces_2_converter_1_z), .a_2(n7_segment_driveri_1_a_2), .b_2(n7_segment_driveri_1_b_2),
    .c_2(n7_segment_driveri_1_c_2), .d_2(n7_segment_driveri_1_d_2), .e(n7_segment_driveri_1_e),
    .f(n7_segment_driveri_1_f), .g(n7_segment_driveri_1_g));
  _7_segment_driveri u_7_segment_driveri_2 (
    .D(_7_as_input[3]), .C(_7_as_input[2]), .B(_7_as_input[1]), .A(_7_as_input[0]),
    .a_2(n7_segment_driveri_2_a_2), .b_2(n7_segment_driveri_2_b_2), .c_2(n7_segment_driveri_2_c_2),
    .d_2(n7_segment_driveri_2_d_2), .e(n7_segment_driveri_2_e), .f(n7_segment_driveri_2_f),
    .g(n7_segment_driveri_2_g));
  _7_Segment_Display u_7_segment_display_1 (
    .g(n7_segment_driveri_1_g), .f(n7_segment_driveri_1_f), .a(n7_segment_driveri_1_a_2),
    .b(n7_segment_driveri_1_b_2), .e(n7_segment_driveri_1_e), .d(n7_segment_driveri_1_d_2),
    .c(n7_segment_driveri_1_c_2));  // open: dp
  _7_Segment_Display u_7_segment_display_2 (
    .g(n7_segment_driveri_2_g), .f(n7_segment_driveri_2_f), .a(n7_segment_driveri_2_a_2),
    .b(n7_segment_driveri_2_b_2), .e(n7_segment_driveri_2_e), .d(n7_segment_driveri_2_d_2),
    .c(n7_segment_driveri_2_c_2));  // open: dp

  // Notes on the sheet:
  //   7 as input
  //   20070001007
endmodule

module Exces_2_converter (
  input  A,
  input  B,
  input  C,
  input  D,
  output W,
  output X,
  output Y,
  output Z
);

  wire and_1_out, and_2_out, and_3_out, not_1_out, not_2_out, not_3_out, not_4_out;

  and and_1 (and_1_out, B, C);
  and and_2 (and_2_out, B, not_1_out);
  not not_1 (not_1_out, C);
  not not_2 (not_2_out, B);
  and and_3 (and_3_out, not_2_out, C);
  not not_3 (not_3_out, C);
  or or_1 (Y, not_3_out, A);
  not not_4 (not_4_out, A);
  and and_4 (Z, not_4_out, D);
  or or_2 (W, A, and_1_out);
  or or_3 (X, and_2_out, and_3_out);
endmodule

module _7_segment_driveri (
  input  D,
  input  C,
  input  B,
  input  A,
  output a_2,
  output b_2,
  output c_2,
  output d_2,
  output e,
  output f,
  output g
);

  wire and_1_out, and_2_out, and_3_out, and_4_out, and_5_out, and_6_out, and_7_out, and_8_out, and_9_out,
       and_10_out, and_11_out, and_12_out, and_13_out, and_14_out, and_15_out, and_16_out, and_17_out,
       and_18_out, and_19_out, and_20_out, and_21_out, and_22_out, and_23_out, and_24_out, and_25_out,
       and_26_out, and_27_out, and_28_out, and_29_out, and_30_out, and_31_out, and_32_out, and_33_out,
       and_34_out, and_35_out, not_1_out, not_2_out, not_3_out, not_4_out, not_5_out, not_6_out, not_7_out,
       not_8_out, not_9_out, not_10_out, not_11_out, not_12_out, not_13_out, not_14_out, not_15_out,
       not_16_out, not_17_out, not_18_out, not_19_out, not_20_out, not_21_out, not_22_out, not_23_out,
       not_24_out, not_25_out, not_26_out, not_27_out, not_28_out, not_29_out, not_30_out, not_31_out,
       not_32_out, not_33_out, not_34_out, not_35_out, not_36_out, not_37_out, not_38_out, not_39_out,
       not_40_out, not_41_out, not_42_out, not_43_out, not_44_out;

  not not_1 (not_1_out, C);
  and and_1 (and_1_out, not_1_out, not_2_out);
  not not_2 (not_2_out, A);
  not not_3 (not_3_out, D);
  and and_2 (and_2_out, not_3_out, B);
  not not_4 (not_4_out, D);
  and and_3 (and_3_out, not_4_out, C, A);
  and and_4 (and_4_out, C, B);
  and and_5 (and_5_out, D, not_5_out, not_6_out);
  not not_5 (not_5_out, C);
  not not_6 (not_6_out, B);
  and and_6 (and_6_out, D, not_7_out);
  not not_7 (not_7_out, A);
  not not_8 (not_8_out, D);
  and and_7 (and_7_out, not_8_out, not_9_out);
  not not_9 (not_9_out, C);
  not not_10 (not_10_out, D);
  and and_8 (and_8_out, not_10_out, not_11_out, not_12_out);
  not not_11 (not_11_out, B);
  not not_12 (not_12_out, A);
  not not_13 (not_13_out, C);
  and and_9 (and_9_out, not_13_out, not_14_out);
  not not_14 (not_14_out, A);
  not not_15 (not_15_out, D);
  and and_10 (and_10_out, not_15_out, B, A);
  not not_16 (not_16_out, B);
  and and_11 (and_11_out, D, not_16_out, A);
  not not_17 (not_17_out, D);
  and and_12 (and_12_out, not_17_out, not_18_out);
  not not_18 (not_18_out, B);
  not not_19 (not_19_out, D);
  and and_13 (and_13_out, not_19_out, A);
  not not_20 (not_20_out, B);
  and and_14 (and_14_out, not_20_out, A);
  not not_21 (not_21_out, D);
  and and_15 (and_15_out, not_21_out, C);
  and and_16 (and_16_out, D, not_22_out);
  not not_22 (not_22_out, C);
  not not_23 (not_23_out, D);
  and and_17 (and_17_out, not_23_out, not_24_out, not_25_out);
  not not_24 (not_24_out, C);
  not not_25 (not_25_out, A);
  not not_26 (not_26_out, C);
  and and_18 (and_18_out, not_26_out, B, A);
  not not_27 (not_27_out, B);
  and and_19 (and_19_out, C, not_27_out, A);
  and and_20 (and_20_out, C, B, not_28_out);
  not not_28 (not_28_out, A);
  and and_21 (and_21_out, D, not_29_out, not_30_out);
  not not_29 (not_29_out, B);
  not not_30 (not_30_out, A);
  not not_31 (not_31_out, C);
  and and_22 (and_22_out, not_31_out, not_32_out);
  not not_32 (not_32_out, A);
  and and_23 (and_23_out, B, not_33_out);
  not not_33 (not_33_out, A);
  and and_24 (and_24_out, D, B);
  and and_25 (and_25_out, D, C);
  not not_34 (not_34_out, B);
  and and_26 (and_26_out, not_34_out, not_35_out);
  not not_35 (not_35_out, A);
  not not_36 (not_36_out, D);
  and and_27 (and_27_out, not_36_out, C, not_37_out);
  not not_37 (not_37_out, B);
  and and_28 (and_28_out, C, not_38_out);
  not not_38 (not_38_out, A);
  and and_29 (and_29_out, D, not_39_out);
  not not_39 (not_39_out, C);
  and and_30 (and_30_out, D, B);
  not not_40 (not_40_out, C);
  and and_31 (and_31_out, not_40_out, B);
  and and_32 (and_32_out, B, not_41_out);
  not not_41 (not_41_out, A);
  not not_42 (not_42_out, D);
  and and_33 (and_33_out, not_42_out, C, not_43_out);
  not not_43 (not_43_out, B);
  and and_34 (and_34_out, D, not_44_out);
  not not_44 (not_44_out, C);
  and and_35 (and_35_out, D, A);
  or or_1 (b_2, and_7_out, and_8_out, and_9_out, and_10_out, and_11_out);
  or or_2 (c_2, and_12_out, and_13_out, and_14_out, and_15_out, and_16_out);
  or or_3 (d_2, and_17_out, and_18_out, and_19_out, and_20_out, and_21_out);
  or or_4 (e, and_22_out, and_23_out, and_24_out, and_25_out);
  or or_5 (f, and_26_out, and_27_out, and_28_out, and_29_out, and_30_out);
  or or_6 (g, and_31_out, and_32_out, and_33_out, and_34_out, and_35_out);
  or or_7 (a_2, and_1_out, and_2_out, and_3_out, and_4_out, and_5_out, and_6_out);
endmodule
